# Fritzing sketch Circuit Disgram (saved by Fritzing 0.8.7b)
breadboards: 1

parts:
  Part1 = Arduino Nano (Rev3.0) (ICSP)
  M1 = DC Motor
  M2 = DC Motor
  M3 = DC Motor
  M4 = DC Motor
  3-Axis_Accelerometer1 = 3-Axis Accelerometer Breakout - MMA8452Q
  VCC1 = Battery block 9V
  U2 = SUP500F [package=sup500f]
  U3 = NodeMCU V1.0
  S1 = H-Bridge with L298N
  S2 = H-Bridge with L298N
  Part2 = SRF05 Ultrasonic Rangefinder
  VCC2 = Battery block 9V
  U4 = LIPO-1000mAh [package=lipo-1000]

nets:
  N1: Part1.D1/TX, U3.RX
  N2: Part1.D0/RX, U3.TX
  GND: Part1.RESET, 3-Axis_Accelerometer1.GND, U2.RX-I, U3.GND, Part2.GND, U4.-
  N3: Part1.GND, 3-Axis_Accelerometer1.I1
  N4: Part1.D2, S2.IN1
  N5: Part1.D3, S2.IN2
  N6: Part1.D4, S2.IN3
  N7: Part1.D5, S2.IN4
  N8: Part1.D6, S1.IN4
  N9: Part1.D7, S1.IN3
  N10: Part1.D8, S1.IN2
  N11: Part1.D9, S1.IN1
  N12: Part1.D10, Part2.Trig
  N13: Part1.D11/MOSI, Part2.Echo
  N14: Part1.VIN, 3-Axis_Accelerometer1.I2
  N15: Part1.A7, 3-Axis_Accelerometer1.SDA
  N16: Part1.A6, 3-Axis_Accelerometer1.SCL
  N17: Part1.A5, S1.ENA
  N18: Part1.A4, S1.ENB
  N19: Part1.A1, S2.ENB
  N20: Part1.A0, S2.ENA
  N21: M1.pin_1, S1.M2-02
  N22: M1.pin_2, S1.M2-01
  N23: M2.pin_1, S2.M1-02
  N24: M2.pin_2, S2.M1-01
  N25: M3.pin_1, S2.M2-02
  N26: M3.pin_2, S2.M2-01
  N27: M4.pin_1, S1.M1-02
  N28: M4.pin_2, S1.M1-01
  VCC: 3-Axis_Accelerometer1.3.3V, U2.VCC, U3.Vin, Part2.VCC, U4.+
  N29: VCC1.-, S2.GND
  N30: VCC1.+, S2.12V
  N31: U2.TX-O, U3.D7
  N32: U2.GND, U3.D6
  N33: S1.12V, VCC2.+
  N34: S1.GND, VCC2.-

custom parts:
  NodeMCU V1.0: ESP8266 based NodeMCU
  H-Bridge with L298N: h-bridge
